// Logisim project ProjectBusLayout (2).circ as structural Verilog: 14 circuits, main circuit Computer
module Computer (
);

  wire buzzercontroller_1_enablesound, clock_1_out, clock_2_out, clock_3_out, clock_5_out,
       cpumain_1_buswriteenable, keyboard_1_avail, keyboardcontroller_1_keyboardread,
       keyboardcontroller_1_writetobus, memorycontroller_1_writeenabletomem, memorycontroller_1_writetobus,
       oscicontroller_1_clear, oscicontroller_1_enablewrite, oscicontroller_1_row1, oscicontroller_1_row2,
       oscicontroller_1_row3, rgb_video_1_p1, rgb_video_1_p2, terminalcontroller_1_writetoterminal;
  wire [4:0] ledmatrixcontroller_1_col1, ledmatrixcontroller_1_col2, ledmatrixcontroller_1_col3,
       ledmatrixcontroller_1_col4, ledmatrixcontroller_1_col5;
  wire [6:0] buzzercontroller_1_volume, keyboard_1_data, speakercontroller_1_v2, speakercontroller_1_v3,
       speakercontroller_1_volume1, terminalcontroller_1_datatoterminal;
  wire [7:0] rgb_video_1_p3, rgb_video_1_p4;
  wire [13:0] buzzercontroller_1_frequency, speakercontroller_1_f2, speakercontroller_1_f3,
       speakercontroller_1_frequency1;
  wire [23:0] memorycontroller_1_addresstomem, rgb_video_1_p5;
  wire [25:0] cpumain_1_addresstobus;
  wire [31:0] controlled_buffer_1_out, cpumain_1_datatobus, keyboardcontroller_1_datatobus,
       memorycontroller_1_datatobus, memorycontroller_1_datatomem, ram_1_dout;

  RAM #(.addrWidth(24), .dataWidth(32), .enables("line")) ram_1 (
    .addr(memorycontroller_1_addresstomem), .we(memorycontroller_1_writeenabletomem), .clk(clock_1_out),
    .din(memorycontroller_1_datatomem), .dout(ram_1_dout));
  Clock clock_1 (.out(clock_1_out));
  Clock clock_2 (.out(clock_2_out));
  Keyboard keyboard_1 (
    .clk(clock_2_out), .re(keyboardcontroller_1_keyboardread), .avail(keyboard_1_avail),
    .data(keyboard_1_data));  // open: clr
  MemoryController memorycontroller_1 (
    .WriteEnableFromBus(cpumain_1_buswriteenable), .AddressFromBus(cpumain_1_addresstobus),
    .DataFromMem(ram_1_dout), .DataFromBus(controlled_buffer_1_out),
    .WriteEnableToMem(memorycontroller_1_writeenabletomem), .DataToBus(memorycontroller_1_datatobus),
    .AddressToMem(memorycontroller_1_addresstomem), .DataToMem(memorycontroller_1_datatomem),
    .WriteToBus(memorycontroller_1_writetobus));
  CPUmain cpumain_1 (
    .DataFromBus(controlled_buffer_1_out), .AddressToBus(cpumain_1_addresstobus),
    .BusWriteEnable(cpumain_1_buswriteenable), .DataToBus(cpumain_1_datatobus));
  assign controlled_buffer_1_out = memorycontroller_1_writetobus ? memorycontroller_1_datatobus : 32'bz;  // Controlled_Buffer controlled_buffer_1
  assign controlled_buffer_1_out = cpumain_1_buswriteenable ? cpumain_1_datatobus : 32'bz;  // Controlled_Buffer controlled_buffer_2
  KeyboardController keyboardcontroller_1 (
    .DataFromBus(controlled_buffer_1_out), .WriteEnableFromBus(cpumain_1_buswriteenable),
    .AddressFromBus(cpumain_1_addresstobus), .KeyboardData(keyboard_1_data),
    .KeyboardStatus(keyboard_1_avail), .DataToBus(keyboardcontroller_1_datatobus),
    .KeyboardRead(keyboardcontroller_1_keyboardread), .WriteToBus(keyboardcontroller_1_writetobus));
  assign controlled_buffer_1_out = keyboardcontroller_1_writetobus ? keyboardcontroller_1_datatobus : 32'bz;  // Controlled_Buffer controlled_buffer_3
  Clock clock_3 (.out(clock_3_out));
  TTY tty_1 (
    .data(terminalcontroller_1_datatoterminal), .clk(clock_3_out), .we(terminalcontroller_1_writetoterminal));  // open: clr
  // RGB_Video #(.height(256), .scale(1), .width(256)) rgb_video_1: pin names not known; wires that end beside it: rgb_video_1_p1, rgb_video_1_p2, rgb_video_1_p3, rgb_video_1_p4, rgb_video_1_p5
  Clock clock_4 (.out(rgb_video_1_p1));
  TerminalController terminalcontroller_1 (
    .WriteEnableFromBus(cpumain_1_buswriteenable), .AddressFromBus(cpumain_1_addresstobus),
    .DataFromBus(controlled_buffer_1_out), .WriteToTerminal(terminalcontroller_1_writetoterminal),
    .DataToTerminal(terminalcontroller_1_datatoterminal));
  RGBController rgbcontroller_1 (
    .AddressFromBus(cpumain_1_addresstobus), .DataFromBus(controlled_buffer_1_out),
    .WriteEnable(cpumain_1_buswriteenable), .RGBX(rgb_video_1_p3), .RGBY(rgb_video_1_p4),
    .RGBColor(rgb_video_1_p5), .RGBWrite(rgb_video_1_p2));
  OsciController oscicontroller_1 (
    .WE(cpumain_1_buswriteenable), .AddressFromBus(cpumain_1_addresstobus),
    .DataFromBus(controlled_buffer_1_out), .Row1(oscicontroller_1_row1), .Row2(oscicontroller_1_row2),
    .Row3(oscicontroller_1_row3), .Clear(oscicontroller_1_clear), .EnableWrite(oscicontroller_1_enablewrite));
  BuzzerController buzzercontroller_1 (
    .DataFromBus(controlled_buffer_1_out), .WEFromBus(cpumain_1_buswriteenable),
    .AddressFromBus(cpumain_1_addresstobus), .Frequency(buzzercontroller_1_frequency),
    .Volume(buzzercontroller_1_volume), .EnableSound(buzzercontroller_1_enablesound));
  LEDMatrixController ledmatrixcontroller_1 (
    .WE(cpumain_1_buswriteenable), .AddressFromBus(cpumain_1_addresstobus),
    .DataFromBus(controlled_buffer_1_out), .Col1(ledmatrixcontroller_1_col1),
    .Col2(ledmatrixcontroller_1_col2), .Col3(ledmatrixcontroller_1_col3), .Col4(ledmatrixcontroller_1_col4),
    .Col5(ledmatrixcontroller_1_col5));
  SpeakerController speakercontroller_1 (
    .DataFromBus(controlled_buffer_1_out), .WEFromBus(cpumain_1_buswriteenable),
    .AddressfromBus(cpumain_1_addresstobus), .Frequency1(speakercontroller_1_frequency1),
    .Volume1(speakercontroller_1_volume1), .F2(speakercontroller_1_f2), .V2(speakercontroller_1_v2),
    .F3(speakercontroller_1_f3), .V3(speakercontroller_1_v3));
  Clock clock_5 (.out(clock_5_out));
  // Digital_Oscilloscope digital_oscilloscope_1: pin names not known; wires that end beside it: clock_5_out, oscicontroller_1_row1, oscicontroller_1_row2, oscicontroller_1_row3, oscicontroller_1_enablewrite, oscicontroller_1_clear
  // Buzzer buzzer_1: pin names not known; wires that end beside it: buzzercontroller_1_frequency, buzzercontroller_1_enablesound, buzzercontroller_1_volume
  DotMatrix #(.matrixrows(5)) dotmatrix_1 (
    .col0(ledmatrixcontroller_1_col1), .col1(ledmatrixcontroller_1_col2), .col2(ledmatrixcontroller_1_col3),
    .col3(ledmatrixcontroller_1_col4), .col4(ledmatrixcontroller_1_col5));
  // Buzzer #(.waveform("Square")) buzzer_2: pin names not known; wires that end beside it: speakercontroller_1_frequency1, 1'b1, speakercontroller_1_volume1
  // Buzzer #(.waveform("Square")) buzzer_3: pin names not known; wires that end beside it: speakercontroller_1_f2, 1'b1, speakercontroller_1_v2
  // Buzzer #(.waveform("Triangle")) buzzer_4: pin names not known; wires that end beside it: speakercontroller_1_f3, 1'b1, speakercontroller_1_v3

  // Notes on the sheet:
  //   Write_enable
  //   Address
  //   Data
endmodule

module MemoryController (
  input  WriteEnableFromBus,
  input  [25:0] AddressFromBus,
  input  [31:0] DataFromBus,
  input  [31:0] DataFromMem,
  output [31:0] DataToBus,
  output WriteToBus,
  output WriteEnableToMem,
  output [23:0] AddressToMem,
  output [31:0] DataToMem
);

  wire comparator_1_lt, not_1_out;
  wire [25:0] shifter_1_out;

  Comparator #(.mode("unsigned"), .width(26)) comparator_1 (
    .a(AddressFromBus), .b(26'h3ffff00), .lt(comparator_1_lt));  // open: gt, eq
  not not_1 (not_1_out, WriteEnableFromBus);
  and and_1 (WriteEnableToMem, WriteEnableFromBus, comparator_1_lt);
  and and_2 (WriteToBus, not_1_out, comparator_1_lt);
  Shifter #(.shift("lr"), .width(26)) shifter_1 (.in(AddressFromBus), .\dist (5'b00010), .out(shifter_1_out));
  Bit_Extender #(.in_width(26), .out_width(24)) bit_extender_1 (.in(shifter_1_out), .out(AddressToMem));

  assign DataToBus = DataFromMem;
  assign DataToMem = DataFromBus;
endmodule

module KeyboardController (
  input  [31:0] DataFromBus,
  input  WriteEnableFromBus,
  input  [25:0] AddressFromBus,
  input  [6:0] KeyboardData,
  input  KeyboardStatus,
  output WriteToBus,
  output [31:0] DataToBus,
  output KeyboardRead
);

  wire and_1_out, and_2_out, comparator_1_eq, comparator_2_eq, controlled_buffer_1_out, not_1_out;
  wire [31:0] bit_extender_1_out, bit_extender_2_out;

  not not_1 (not_1_out, WriteEnableFromBus);
  Comparator #(.width(26)) comparator_1 (.a(AddressFromBus), .b(26'h3ffff10), .eq(comparator_1_eq));  // open: gt, lt
  Comparator #(.width(26)) comparator_2 (.a(AddressFromBus), .b(26'h3ffff14), .eq(comparator_2_eq));  // open: gt, lt
  and and_1 (and_1_out, comparator_1_eq, not_1_out);
  and and_2 (and_2_out, not_1_out, comparator_2_eq);
  and and_3 (KeyboardRead, WriteEnableFromBus, comparator_1_eq);
  or or_1 (WriteToBus, and_1_out, and_2_out);
  assign controlled_buffer_1_out = and_1_out ? KeyboardStatus : 1'bz;  // Controlled_Buffer controlled_buffer_1
  assign bit_extender_1_out = {{31{1'b0}}, controlled_buffer_1_out};  // Bit_Extender bit_extender_1
  assign bit_extender_2_out = {{25{1'b0}}, KeyboardData};  // Bit_Extender bit_extender_2
  Multiplexer #(.width(32)) multiplexer_1 (
    .in0(bit_extender_1_out), .in1(bit_extender_2_out), .out(DataToBus), .sel(and_2_out));
endmodule

module RGBController (
  input  [25:0] AddressFromBus,
  input  [31:0] DataFromBus,
  input  WriteEnable,
  output [7:0] RGBX,
  output [7:0] RGBY,
  output [23:0] RGBColor,
  output RGBWrite
);

  wire and_1_out, and_2_out, and_3_out, clock_1_out, comparator_1_eq, comparator_2_eq, comparator_3_eq,
       comparator_4_eq;
  wire [7:0] bit_extender_2_out;
  wire [23:0] bit_extender_1_out;

  Comparator #(.width(26)) comparator_1 (.a(AddressFromBus), .b(26'h3ffff20), .eq(comparator_1_eq));  // open: gt, lt
  Comparator #(.width(26)) comparator_2 (.a(AddressFromBus), .b(26'h3ffff24), .eq(comparator_2_eq));  // open: gt, lt
  Comparator #(.width(26)) comparator_3 (.a(AddressFromBus), .b(26'h3ffff28), .eq(comparator_3_eq));  // open: gt, lt
  Comparator #(.width(26)) comparator_4 (.a(AddressFromBus), .b(26'h3ffff2c), .eq(comparator_4_eq));  // open: gt, lt
  Bit_Extender #(.in_width(32), .out_width(24)) bit_extender_1 (.in(DataFromBus), .out(bit_extender_1_out));
  Bit_Extender #(.in_width(24), .out_width(8)) bit_extender_2 (.in(bit_extender_1_out), .out(bit_extender_2_out));
  Clock clock_1 (.out(clock_1_out));
  Register X (.D(bit_extender_2_out), .en(and_1_out), .clk(clock_1_out), .Q(RGBX));  // open: clr
  and and_1 (and_1_out, comparator_1_eq, WriteEnable);
  Register Y (.D(bit_extender_2_out), .en(and_2_out), .clk(clock_1_out), .Q(RGBY));  // open: clr
  and and_2 (and_2_out, comparator_2_eq, WriteEnable);
  Register #(.width(24)) Color (.D(bit_extender_1_out), .en(and_3_out), .clk(clock_1_out), .Q(RGBColor));  // open: clr
  and and_3 (and_3_out, comparator_3_eq, WriteEnable);
  and and_4 (RGBWrite, comparator_4_eq, WriteEnable);

  // Notes on the sheet:
  //   X
  //   Y
  //   Color
  //   WE
endmodule

module TerminalController (
  input  WriteEnableFromBus,
  input  [25:0] AddressFromBus,
  input  [31:0] DataFromBus,
  output WriteToTerminal,
  output [6:0] DataToTerminal
);

  wire comparator_1_eq;

  Comparator #(.width(26)) comparator_1 (.a(AddressFromBus), .b(26'h3ffff00), .eq(comparator_1_eq));  // open: gt, lt
  Bit_Extender #(.in_width(32), .out_width(7)) bit_extender_1 (.in(DataFromBus), .out(DataToTerminal));
  and and_1 (WriteToTerminal, WriteEnableFromBus, comparator_1_eq);
endmodule

module CPUmain (
  input  [31:0] DataFromBus,
  output [25:0] AddressToBus,
  output BusWriteEnable,
  output [31:0] DataToBus
);

  wire alu_1_equal, clock_1_out, control_1_imm_sel, control_1_isj, control_1_isjal, control_1_isjr,
       control_1_mem_load, control_1_reg_write_e;
  wire [3:0] control_1_alu_code;
  wire [4:0] control_1_rd, control_1_rs, control_1_rt, control_1_shamt;
  wire [15:0] bit_extender_2_out;
  wire [25:0] bit_extender_3_out, shifter_2_out;
  wire [31:0] adder_1_out, adder_2_out, alu_1_res, bit_extender_1_out, control_1_imm, multiplexer_1_out,
       multiplexer_2_out, multiplexer_3_out, multiplexer_4_out, multiplexer_5_out, multiplexer_6_out,
       regfile_1_rs_data, register_1_q, rom_1_data, shifter_1_out, shifter_3_out;

  Shifter #(.width(32)) shifter_1 (.in(control_1_imm), .\dist (5'b00010), .out(shifter_1_out));
  Adder #(.width(32)) adder_1 (.a(register_1_q), .b(32'h4), .out(adder_1_out));  // open: cin, cout
  Shifter #(.width(26)) shifter_2 (.in(bit_extender_3_out), .\dist (5'b00010), .out(shifter_2_out));
  Multiplexer #(.width(32)) multiplexer_1 (
    .in0(adder_1_out), .in1(adder_2_out), .out(multiplexer_1_out), .sel(alu_1_equal));
  Adder #(.width(32)) adder_2 (.a(adder_1_out), .b(shifter_1_out), .out(adder_2_out));  // open: cin, cout
  assign bit_extender_1_out = {{6{shifter_2_out[25]}}, shifter_2_out};  // Bit_Extender bit_extender_1
  Multiplexer #(.width(32)) multiplexer_2 (
    .in0(bit_extender_1_out), .in1(regfile_1_rs_data), .out(multiplexer_2_out), .sel(control_1_isjr));
  Multiplexer #(.width(32)) multiplexer_3 (
    .in0(multiplexer_1_out), .in1(multiplexer_2_out), .out(multiplexer_3_out), .sel(control_1_isj));
  Shifter #(.shift("lr"), .width(32)) shifter_3 (.in(register_1_q), .\dist (5'b00010), .out(shifter_3_out));
  Bit_Extender #(.in_width(32)) bit_extender_2 (.in(shifter_3_out), .out(bit_extender_2_out));
  Register #(.width(32)) register_1 (
    .D(multiplexer_3_out), .en(1'b1), .clk(clock_1_out), .Q(register_1_q));  // open: clr
  Clock clock_1 (.out(clock_1_out));
  ROM #(.addrWidth(16), .dataWidth(32)) rom_1 (.addr(bit_extender_2_out), .data(rom_1_data));
  Bit_Extender #(.in_width(32), .out_width(26)) bit_extender_3 (.in(rom_1_data), .out(bit_extender_3_out));
  Multiplexer #(.width(32)) multiplexer_4 (
    .in0(alu_1_res), .in1(DataFromBus), .out(multiplexer_4_out), .sel(control_1_mem_load));
  Multiplexer #(.width(32)) multiplexer_5 (
    .in0(multiplexer_4_out), .in1(adder_1_out), .out(multiplexer_5_out), .sel(control_1_isjal));
  regfile regfile_1 (
    .write_e(control_1_reg_write_e), .rd_data(multiplexer_5_out), .rs(control_1_rs), .rt(control_1_rt),
    .rd(control_1_rd), .rs_data(regfile_1_rs_data), .rt_data(DataToBus));
  Control control_1 (
    .Inst(rom_1_data), .isjr(control_1_isjr), .isjal(control_1_isjal), .imm(control_1_imm),
    .ALU_code(control_1_alu_code), .reg_write_e(control_1_reg_write_e), .shamt(control_1_shamt),
    .rt(control_1_rt), .rd(control_1_rd), .rs(control_1_rs), .imm_sel(control_1_imm_sel),
    .mem_load(control_1_mem_load), .mem_write_e(BusWriteEnable), .isj(control_1_isj));
  Multiplexer #(.width(32)) multiplexer_6 (
    .in0(DataToBus), .in1(control_1_imm), .out(multiplexer_6_out), .sel(control_1_imm_sel));
  ALU alu_1 (
    .ALU_CODE(control_1_alu_code), .OP1(regfile_1_rs_data), .OP2(multiplexer_6_out), .shamt(control_1_shamt),
    .Res(alu_1_res), .equal(alu_1_equal));
  Bit_Extender #(.in_width(32), .out_width(26)) bit_extender_4 (.in(alu_1_res), .out(AddressToBus));
  Clock clock_2 ();  // open: out

  // Notes on the sheet:
  //   contents of rom_1 (hex, n*v repeats v):
  //   1040000d 201b0001 105b000f 201b0005 105b0030 201b0009 105b0055 201b000a 105b0058 201b000b 105b0057
  //   201b000c 105b0057 8000061 23bdf000 201b0000 ac1bf004 800006a 23bdfff8 afa80000 afa90004 20090000
  //   14800003 20080030 ac08ff00 8000031 80402a 11000005 2008002d ac08ff00 2008ffff 1040018 2012 2008000a
  //   88001a 2012 4010 10800004 21290001 23bdfffc afa80000 8000021 21080030 ac08ff00 11200004 8fa80000
  //   23bd0004 2129ffff 800002a 8fa80000 8fa90004 23bd0008 3400008 23bdfff0 afa80000 afa90004 afaa0008
  //   afab000c 200b0001 8c08ff10 1100fffe 8c08ff14 20020000 2009002d 15090003 ac00ff10 200bffff 800003b
  //   8c08ff14 2009003a 109502a 1140000c 20090030 109502a 15400009 200a000a 1420018 1012 2108ffd0 481020
  //   ac00ff10 8c08ff10 1100fffe 8000044 1620018 1012 8fa80000 8fa90004 8faa0008 8fab000c 23bd0010 3400008
  //   8c1bf004 364d820 23620000 ac1bf004 3400008 8000061 ac04ff00 3400008 8c02ff10 14400001 8000064
  //   8c02ff14 ac00ff10 3400008 2010005f 2011002b 2012002d 2013002f 2014002a 20160025 20170000 20020005
  //   d009 20480000 2002000c d009 20490000 1130000b 20020005 d009 204a0000 2002000c d009 11300014 1131001b
  //   1132001f 11330023 11340028 1136002d 22e80000 2002000c d009 20490000 20020005 d009 204a0000 2002000c
  //   d009 11300005 1131000c 11320010 11330014 11340019 1136001e 2002000c d009 22ea0000 11310004 11320008
  //   1133000c 11340011 11360016 10ab820 20020001 22e40000 d009 8000071 10ab822 20020001 22e40000 d009
  //   8000071 10a001a b812 20020001 22e40000 d009 8000071 1480018 b812 20020001 22e40000 d009 8000071
  //   10a001a b810 20020001 22e40000 d009 8000071
endmodule

module regfile (
  input  write_e,
  input  [4:0] rd,
  input  [4:0] rs,
  input  [31:0] rd_data,
  input  [4:0] rt,
  output [31:0] rs_data,
  output [31:0] rt_data
);

  wire clock_1_out, demultiplexer_1_out1, demultiplexer_1_out2, demultiplexer_1_out3, demultiplexer_1_out4,
       demultiplexer_1_out5, demultiplexer_1_out6, demultiplexer_1_out7, demultiplexer_1_out8,
       demultiplexer_1_out9, demultiplexer_1_out10, demultiplexer_1_out11, demultiplexer_1_out12,
       demultiplexer_1_out13, demultiplexer_1_out14, demultiplexer_1_out15, demultiplexer_1_out16,
       demultiplexer_1_out17, demultiplexer_1_out18, demultiplexer_1_out19, demultiplexer_1_out20,
       demultiplexer_1_out21, demultiplexer_1_out22, demultiplexer_1_out23, demultiplexer_1_out24,
       demultiplexer_1_out25, demultiplexer_1_out26, demultiplexer_1_out27, demultiplexer_1_out28,
       demultiplexer_1_out29, demultiplexer_1_out30, demultiplexer_1_out31;
  wire [31:0] demultiplexer_2_out1, demultiplexer_2_out2, demultiplexer_2_out3, demultiplexer_2_out4,
       demultiplexer_2_out5, demultiplexer_2_out6, demultiplexer_2_out7, demultiplexer_2_out8,
       demultiplexer_2_out9, demultiplexer_2_out10, demultiplexer_2_out11, demultiplexer_2_out12,
       demultiplexer_2_out13, demultiplexer_2_out14, demultiplexer_2_out15, demultiplexer_2_out16,
       demultiplexer_2_out17, demultiplexer_2_out18, demultiplexer_2_out19, demultiplexer_2_out20,
       demultiplexer_2_out21, demultiplexer_2_out22, demultiplexer_2_out23, demultiplexer_2_out24,
       demultiplexer_2_out25, demultiplexer_2_out26, demultiplexer_2_out27, demultiplexer_2_out28,
       demultiplexer_2_out29, demultiplexer_2_out30, demultiplexer_2_out31, Reg1_q, Reg2_q, Reg3_q, Reg4_q,
       Reg5_q, Reg6_q, Reg7_q, Reg8_q, Reg9_q, Reg10_q, Reg11_q, Reg12_q, Reg13_q, Reg14_q, Reg15_q, Reg16_q,
       Reg17_q, Reg18_q, Reg19_q, Reg20_q, Reg21_q, Reg22_q, Reg23_q, Reg24_q, Reg25_q, Reg26_q, Reg27_q,
       Reg28_q, Reg29_q, Reg30_q, Reg31_q;

  Demultiplexer #(.select(5)) demultiplexer_1 (
    .out1(demultiplexer_1_out1), .out2(demultiplexer_1_out2), .out3(demultiplexer_1_out3),
    .out4(demultiplexer_1_out4), .out5(demultiplexer_1_out5), .out6(demultiplexer_1_out6),
    .out7(demultiplexer_1_out7), .out8(demultiplexer_1_out8), .out9(demultiplexer_1_out9),
    .out10(demultiplexer_1_out10), .out11(demultiplexer_1_out11), .out12(demultiplexer_1_out12),
    .out13(demultiplexer_1_out13), .out14(demultiplexer_1_out14), .out15(demultiplexer_1_out15),
    .out16(demultiplexer_1_out16), .out17(demultiplexer_1_out17), .out18(demultiplexer_1_out18),
    .out19(demultiplexer_1_out19), .out20(demultiplexer_1_out20), .out21(demultiplexer_1_out21),
    .out22(demultiplexer_1_out22), .out23(demultiplexer_1_out23), .out24(demultiplexer_1_out24),
    .out25(demultiplexer_1_out25), .out26(demultiplexer_1_out26), .out27(demultiplexer_1_out27),
    .out28(demultiplexer_1_out28), .out29(demultiplexer_1_out29), .out30(demultiplexer_1_out30),
    .out31(demultiplexer_1_out31), .in(write_e), .sel(rd));  // open: out0
  Demultiplexer #(.select(5), .width(32)) demultiplexer_2 (
    .out1(demultiplexer_2_out1), .out2(demultiplexer_2_out2), .out3(demultiplexer_2_out3),
    .out4(demultiplexer_2_out4), .out5(demultiplexer_2_out5), .out6(demultiplexer_2_out6),
    .out7(demultiplexer_2_out7), .out8(demultiplexer_2_out8), .out9(demultiplexer_2_out9),
    .out10(demultiplexer_2_out10), .out11(demultiplexer_2_out11), .out12(demultiplexer_2_out12),
    .out13(demultiplexer_2_out13), .out14(demultiplexer_2_out14), .out15(demultiplexer_2_out15),
    .out16(demultiplexer_2_out16), .out17(demultiplexer_2_out17), .out18(demultiplexer_2_out18),
    .out19(demultiplexer_2_out19), .out20(demultiplexer_2_out20), .out21(demultiplexer_2_out21),
    .out22(demultiplexer_2_out22), .out23(demultiplexer_2_out23), .out24(demultiplexer_2_out24),
    .out25(demultiplexer_2_out25), .out26(demultiplexer_2_out26), .out27(demultiplexer_2_out27),
    .out28(demultiplexer_2_out28), .out29(demultiplexer_2_out29), .out30(demultiplexer_2_out30),
    .out31(demultiplexer_2_out31), .in(rd_data), .sel(rd));  // open: out0
  Clock clock_1 (.out(clock_1_out));
  Register #(.width(32)) Reg1 (
    .D(demultiplexer_2_out1), .en(demultiplexer_1_out1), .clk(clock_1_out), .Q(Reg1_q));  // open: clr
  Register #(.width(32)) Reg2 (
    .D(demultiplexer_2_out2), .en(demultiplexer_1_out2), .clk(clock_1_out), .Q(Reg2_q));  // open: clr
  Register #(.width(32)) Reg3 (
    .D(demultiplexer_2_out3), .en(demultiplexer_1_out3), .clk(clock_1_out), .Q(Reg3_q));  // open: clr
  Register #(.width(32)) Reg4 (
    .D(demultiplexer_2_out4), .en(demultiplexer_1_out4), .clk(clock_1_out), .Q(Reg4_q));  // open: clr
  Register #(.width(32)) Reg5 (
    .D(demultiplexer_2_out5), .en(demultiplexer_1_out5), .clk(clock_1_out), .Q(Reg5_q));  // open: clr
  Register #(.width(32)) Reg6 (
    .D(demultiplexer_2_out6), .en(demultiplexer_1_out6), .clk(clock_1_out), .Q(Reg6_q));  // open: clr
  Register #(.width(32)) Reg7 (
    .D(demultiplexer_2_out7), .en(demultiplexer_1_out7), .clk(clock_1_out), .Q(Reg7_q));  // open: clr
  Register #(.width(32)) Reg8 (
    .D(demultiplexer_2_out8), .en(demultiplexer_1_out8), .clk(clock_1_out), .Q(Reg8_q));  // open: clr
  Register #(.width(32)) Reg9 (
    .D(demultiplexer_2_out9), .en(demultiplexer_1_out9), .clk(clock_1_out), .Q(Reg9_q));  // open: clr
  Register #(.width(32)) Reg10 (
    .D(demultiplexer_2_out10), .en(demultiplexer_1_out10), .clk(clock_1_out), .Q(Reg10_q));  // open: clr
  Register #(.width(32)) Reg11 (
    .D(demultiplexer_2_out11), .en(demultiplexer_1_out11), .clk(clock_1_out), .Q(Reg11_q));  // open: clr
  Register #(.width(32)) Reg12 (
    .D(demultiplexer_2_out12), .en(demultiplexer_1_out12), .clk(clock_1_out), .Q(Reg12_q));  // open: clr
  Register #(.width(32)) Reg13 (
    .D(demultiplexer_2_out13), .en(demultiplexer_1_out13), .clk(clock_1_out), .Q(Reg13_q));  // open: clr
  Register #(.width(32)) Reg14 (
    .D(demultiplexer_2_out14), .en(demultiplexer_1_out14), .clk(clock_1_out), .Q(Reg14_q));  // open: clr
  Register #(.width(32)) Reg15 (
    .D(demultiplexer_2_out15), .en(demultiplexer_1_out15), .clk(clock_1_out), .Q(Reg15_q));  // open: clr
  Register #(.width(32)) Reg16 (
    .D(demultiplexer_2_out16), .en(demultiplexer_1_out16), .clk(clock_1_out), .Q(Reg16_q));  // open: clr
  Register #(.width(32)) Reg17 (
    .D(demultiplexer_2_out17), .en(demultiplexer_1_out17), .clk(clock_1_out), .Q(Reg17_q));  // open: clr
  Register #(.width(32)) Reg18 (
    .D(demultiplexer_2_out18), .en(demultiplexer_1_out18), .clk(clock_1_out), .Q(Reg18_q));  // open: clr
  Register #(.width(32)) Reg19 (
    .D(demultiplexer_2_out19), .en(demultiplexer_1_out19), .clk(clock_1_out), .Q(Reg19_q));  // open: clr
  Register #(.width(32)) Reg20 (
    .D(demultiplexer_2_out20), .en(demultiplexer_1_out20), .clk(clock_1_out), .Q(Reg20_q));  // open: clr
  Register #(.width(32)) Reg21 (
    .D(demultiplexer_2_out21), .en(demultiplexer_1_out21), .clk(clock_1_out), .Q(Reg21_q));  // open: clr
  Register #(.width(32)) Reg22 (
    .D(demultiplexer_2_out22), .en(demultiplexer_1_out22), .clk(clock_1_out), .Q(Reg22_q));  // open: clr
  Register #(.width(32)) Reg23 (
    .D(demultiplexer_2_out23), .en(demultiplexer_1_out23), .clk(clock_1_out), .Q(Reg23_q));  // open: clr
  Register #(.width(32)) Reg24 (
    .D(demultiplexer_2_out24), .en(demultiplexer_1_out24), .clk(clock_1_out), .Q(Reg24_q));  // open: clr
  Register #(.width(32)) Reg25 (
    .D(demultiplexer_2_out25), .en(demultiplexer_1_out25), .clk(clock_1_out), .Q(Reg25_q));  // open: clr
  Register #(.width(32)) Reg26 (
    .D(demultiplexer_2_out26), .en(demultiplexer_1_out26), .clk(clock_1_out), .Q(Reg26_q));  // open: clr
  Register #(.width(32)) Reg27 (
    .D(demultiplexer_2_out27), .en(demultiplexer_1_out27), .clk(clock_1_out), .Q(Reg27_q));  // open: clr
  Register #(.width(32)) Reg28 (
    .D(demultiplexer_2_out28), .en(demultiplexer_1_out28), .clk(clock_1_out), .Q(Reg28_q));  // open: clr
  Register #(.width(32)) Reg29 (
    .D(demultiplexer_2_out29), .en(demultiplexer_1_out29), .clk(clock_1_out), .Q(Reg29_q));  // open: clr
  Register #(.width(32)) Reg30 (
    .D(demultiplexer_2_out30), .en(demultiplexer_1_out30), .clk(clock_1_out), .Q(Reg30_q));  // open: clr
  Register #(.width(32)) Reg31 (
    .D(demultiplexer_2_out31), .en(demultiplexer_1_out31), .clk(clock_1_out), .Q(Reg31_q));  // open: clr
  Multiplexer #(.select(5), .width(32)) multiplexer_1 (
    .in0({32{1'b0}}), .in1(Reg1_q), .in2(Reg2_q), .in3(Reg3_q), .in4(Reg4_q), .in5(Reg5_q), .in6(Reg6_q),
    .in7(Reg7_q), .in8(Reg8_q), .in9(Reg9_q), .in10(Reg10_q), .in11(Reg11_q), .in12(Reg12_q), .in13(Reg13_q),
    .in14(Reg14_q), .in15(Reg15_q), .in16(Reg16_q), .in17(Reg17_q), .in18(Reg18_q), .in19(Reg19_q),
    .in20(Reg20_q), .in21(Reg21_q), .in22(Reg22_q), .in23(Reg23_q), .in24(Reg24_q), .in25(Reg25_q),
    .in26(Reg26_q), .in27(Reg27_q), .in28(Reg28_q), .in29(Reg29_q), .in30(Reg30_q), .in31(Reg31_q),
    .out(rs_data), .sel(rs));
  Multiplexer #(.select(5), .width(32)) multiplexer_2 (
    .in0({32{1'b0}}), .in1(Reg1_q), .in2(Reg2_q), .in3(Reg3_q), .in4(Reg4_q), .in5(Reg5_q), .in6(Reg6_q),
    .in7(Reg7_q), .in8(Reg8_q), .in9(Reg9_q), .in10(Reg10_q), .in11(Reg11_q), .in12(Reg12_q), .in13(Reg13_q),
    .in14(Reg14_q), .in15(Reg15_q), .in16(Reg16_q), .in17(Reg17_q), .in18(Reg18_q), .in19(Reg19_q),
    .in20(Reg20_q), .in21(Reg21_q), .in22(Reg22_q), .in23(Reg23_q), .in24(Reg24_q), .in25(Reg25_q),
    .in26(Reg26_q), .in27(Reg27_q), .in28(Reg28_q), .in29(Reg29_q), .in30(Reg30_q), .in31(Reg31_q),
    .out(rt_data), .sel(rt));
endmodule

module ALU (
  input  [3:0] ALU_CODE,
  input  [31:0] OP1,
  input  [31:0] OP2,
  input  [4:0] shamt,
  output [31:0] Res,
  output equal
);

  wire and_1_out, and_2_out, clock_1_out, comparator_1_eq, comparator_1_lt, comparator_2_eq, comparator_3_eq,
       comparator_4_eq, comparator_5_eq, not_1_out, or_3_out;
  wire [31:0] adder_1_out, and_3_out, bit_extender_1_out, divider_1_out, divider_1_rem, HI_q, LO_q,
       multiplexer_1_out, multiplexer_2_out, multiplier_1_cout, multiplier_1_out, not_2_out, or_2_out,
       shifter_1_out, shifter_2_out, subtractor_1_out, xor_1_out;

  Comparator #(.width(32)) comparator_1 (.a(OP1), .b(OP2), .eq(comparator_1_eq), .lt(comparator_1_lt));  // open: gt
  and and_1 (and_1_out, comparator_1_eq, comparator_2_eq);
  Comparator #(.mode("unsigned"), .width(4)) comparator_2 (
    .a(ALU_CODE), .b(4'b1101), .eq(comparator_2_eq));  // open: gt, lt
  Comparator #(.mode("unsigned"), .width(4)) comparator_3 (
    .a(4'b1110), .b(ALU_CODE), .eq(comparator_3_eq));  // open: gt, lt
  and and_2 (and_2_out, comparator_3_eq, not_1_out);
  not not_1 (not_1_out, comparator_1_eq);
  Adder #(.width(32)) adder_1 (.a(OP1), .b(OP2), .out(adder_1_out));  // open: cin, cout
  Subtractor #(.width(32)) subtractor_1 (.a(OP1), .b(OP2), .out(subtractor_1_out));  // open: bin, bout
  Multiplier #(.width(32)) multiplier_1 (
    .a(OP1), .b(OP2), .out(multiplier_1_out), .cout(multiplier_1_cout));  // open: cin
  Divider #(.width(32)) divider_1 (.a(OP1), .b(OP2), .out(divider_1_out), .rem(divider_1_rem));  // open: upper
  Shifter #(.width(32)) shifter_1 (.in(OP2), .\dist (shamt), .out(shifter_1_out));
  Shifter #(.shift("lr"), .width(32)) shifter_2 (.in(OP2), .\dist (shamt), .out(shifter_2_out));
  or or_1 (equal, and_1_out, and_2_out);
  assign and_3_out = OP1 & OP2;  // AND_Gate and_3, 32 bits wide
  assign or_2_out = OP1 | OP2;  // OR_Gate or_2, 32 bits wide
  assign xor_1_out = OP1 ^ OP2;  // XOR_Gate xor_1, 32 bits wide
  Multiplexer #(.select(4), .width(32)) multiplexer_1 (
    .in2(multiplier_1_out), .in3(divider_1_out), .out(multiplexer_1_out), .sel(ALU_CODE));  // open: in0, in1, in4, in5, in6, in7, in8, in9, in10, in11, in12, in13, in14, in15
  Multiplexer #(.select(4), .width(32)) multiplexer_2 (
    .in2(multiplier_1_cout), .in3(divider_1_rem), .out(multiplexer_2_out), .sel(ALU_CODE));  // open: in0, in1, in4, in5, in6, in7, in8, in9, in10, in11, in12, in13, in14, in15
  assign not_2_out = ~or_2_out;  // NOT_Gate not_2, 32 bits wide
  Comparator #(.mode("unsigned"), .width(4)) comparator_4 (
    .a(ALU_CODE), .b(4'b0010), .eq(comparator_4_eq));  // open: gt, lt
  Comparator #(.mode("unsigned"), .width(4)) comparator_5 (
    .a(ALU_CODE), .b(4'b0011), .eq(comparator_5_eq));  // open: gt, lt
  Clock clock_1 (.out(clock_1_out));
  or or_3 (or_3_out, comparator_4_eq, comparator_5_eq);
  Register #(.width(32)) LO (.D(multiplexer_1_out), .en(or_3_out), .clk(clock_1_out), .Q(LO_q));  // open: clr
  Register #(.width(32)) HI (.D(multiplexer_2_out), .en(or_3_out), .clk(clock_1_out), .Q(HI_q));  // open: clr
  assign bit_extender_1_out = {{31{1'b0}}, comparator_1_lt};  // Bit_Extender bit_extender_1
  Multiplexer #(.select(4), .width(32)) multiplexer_3 (
    .in0(adder_1_out), .in1(subtractor_1_out), .in4(LO_q), .in5(HI_q), .in6(shifter_1_out),
    .in7(shifter_2_out), .in8(bit_extender_1_out), .in9(and_3_out), .in10(or_2_out), .in11(xor_1_out),
    .in12(not_2_out), .out(Res), .sel(ALU_CODE));  // open: in2, in3, in13, in14, in15
endmodule

module Control (
  input  [31:0] Inst,
  output isjr,
  output isjal,
  output [31:0] imm,
  output [3:0] ALU_code,
  output reg_write_e,
  output [4:0] shamt,
  output [4:0] rt,
  output [4:0] rd,
  output [4:0] rs,
  output imm_sel,
  output mem_load,
  output mem_write_e,
  output isj
);

  wire comparator_1_eq, comparator_2_eq, comparator_3_eq, comparator_4_eq, comparator_5_eq, comparator_6_eq,
       comparator_9_eq, comparator_10_eq, not_1_out, not_2_out, not_3_out, not_4_out, or_1_out, or_2_out,
       or_3_out, or_4_out;
  wire [4:0] multiplexer_2_out, multiplexer_3_out, multiplexer_4_out, multiplexer_5_out, multiplexer_6_out,
       multiplexer_7_out;

  Comparator #(.mode("unsigned"), .width(6)) comparator_1 (
    .a(6'b000100), .b(Inst[31:26]), .eq(comparator_1_eq));  // open: gt, lt
  Comparator #(.mode("unsigned"), .width(6)) comparator_2 (
    .a(6'b000101), .b(Inst[31:26]), .eq(comparator_2_eq));  // open: gt, lt
  or or_1 (or_1_out, comparator_1_eq, comparator_2_eq);
  not not_1 (not_1_out, or_1_out);
  Comparator #(.mode("unsigned"), .width(6)) comparator_3 (
    .a(6'b001000), .b(Inst[5:0]), .eq(comparator_3_eq));  // open: gt, lt
  Comparator #(.mode("unsigned"), .width(6)) comparator_4 (
    .a(Inst[5:0]), .b(6'b001001), .eq(comparator_4_eq));  // open: gt, lt
  Comparator #(.width(6)) comparator_5 (.a(Inst[5:0]), .b(6'b001100), .eq(comparator_5_eq));  // open: gt, lt
  Comparator #(.mode("unsigned"), .width(6)) comparator_6 (
    .a(Inst[31:26]), .b({6{1'b0}}), .eq(comparator_6_eq));  // open: gt, lt
  or or_2 (or_2_out, comparator_3_eq, comparator_4_eq);
  or or_3 (or_3_out, comparator_4_eq, comparator_5_eq, comparator_10_eq);
  not not_2 (not_2_out, comparator_6_eq);
  Comparator #(.mode("unsigned"), .width(6)) comparator_7 (
    .a(6'b100011), .b(Inst[31:26]), .eq(mem_load));  // open: gt, lt
  Comparator #(.mode("unsigned"), .width(6)) comparator_8 (
    .a(6'b101011), .b(Inst[31:26]), .eq(mem_write_e));  // open: gt, lt
  Comparator #(.mode("unsigned"), .width(6)) comparator_9 (
    .a(6'b000010), .b(Inst[31:26]), .eq(comparator_9_eq));  // open: gt, lt
  Comparator #(.mode("unsigned"), .width(6)) comparator_10 (
    .a(Inst[31:26]), .b(6'b000011), .eq(comparator_10_eq));  // open: gt, lt
  and and_1 (isjr, comparator_6_eq, or_2_out);
  and and_2 (isjal, comparator_6_eq, or_3_out);
  assign imm = {{16{Inst[15]}}, Inst[15:0]};  // Bit_Extender bit_extender_1
  Multiplexer #(.width(5)) multiplexer_1 (.in0(Inst[15:11]), .in1(Inst[20:16]), .out(rd), .sel(not_2_out));
  and and_3 (imm_sel, not_1_out, not_2_out);
  or or_4 (or_4_out, comparator_9_eq, comparator_10_eq);
  or or_5 (isj, isjr, or_4_out);
  Multiplexer #(.enable("true"), .select(5), .width(5)) multiplexer_2 (
    .in0(5'b10000), .in2(5'b10001), .in4(5'b11001), .in5(5'b11010), .in6(5'b11011), .in7(5'b11100),
    .in10(5'b11000), .in12(5'b10000), .out(multiplexer_2_out), .sel(Inst[4:0]), .en(Inst[5]));  // open: in1, in3, in8, in9, in11, in13, in14, in15, in16, in17, in18, in19, in20, in21, in22, in23, in24, in25, in26, in27, in28, in29, in30, in31
  not not_3 (not_3_out, Inst[5]);
  Multiplexer #(.enable("true"), .select(5), .width(5)) multiplexer_3 (
    .in0(5'b10110), .in2(5'b10111), .in9(5'b10000), .in16(5'b10101), .in18(5'b10100), .in24(5'b00010),
    .in26(5'b00011), .out(multiplexer_3_out), .sel(Inst[4:0]), .en(not_3_out));  // open: in1, in3, in4, in5, in6, in7, in8, in10, in11, in12, in13, in14, in15, in17, in19, in20, in21, in22, in23, in25, in27, in28, in29, in30, in31
  Multiplexer #(.enable("true"), .select(5), .width(5)) multiplexer_4 (
    .in3(5'b10000), .in11({5{1'b0}}), .out(multiplexer_4_out), .sel(Inst[30:26]), .en(Inst[31]));  // open: in0, in1, in2, in4, in5, in6, in7, in8, in9, in10, in12, in13, in14, in15, in16, in17, in18, in19, in20, in21, in22, in23, in24, in25, in26, in27, in28, in29, in30, in31
  not not_4 (not_4_out, Inst[31]);
  Multiplexer #(.enable("true"), .select(5), .width(5)) multiplexer_5 (
    .in3(5'b10000), .in4(5'b01101), .in5(5'b01110), .in8(5'b10000), .out(multiplexer_5_out),
    .sel(Inst[30:26]), .en(not_4_out));  // open: in0, in1, in2, in6, in7, in9, in10, in11, in12, in13, in14, in15, in16, in17, in18, in19, in20, in21, in22, in23, in24, in25, in26, in27, in28, in29, in30, in31
  Multiplexer #(.width(5)) multiplexer_6 (
    .in0(multiplexer_2_out), .in1(multiplexer_3_out), .out(multiplexer_6_out), .sel(not_3_out));
  Multiplexer #(.width(5)) multiplexer_7 (
    .in0(multiplexer_4_out), .in1(multiplexer_5_out), .out(multiplexer_7_out), .sel(not_4_out));
  Multiplexer #(.width(5)) multiplexer_8 (
    .in0(multiplexer_6_out), .in1(multiplexer_7_out), .out({reg_write_e, ALU_code}), .sel(not_2_out));

  assign rs = Inst[25:21];
  assign rt = Inst[20:16];
  assign shamt = Inst[10:6];

  // Notes on the sheet:
  //   beq
  //   bne
  //   jr
  //   jalr
  //   syscall
  //   lw
  //   sw
  //   j
  //   jal
  //   jal
  //   or
  //   nor
  //   syscall
  //   jalr
  //   bne
  //   add
  //   sub
  //   and
  //   xor
  //   slt
  //   sll
  //   srl
  //   mfhi
  //   mflo
  //   mult
  //   div
  //   lw
  //   sw
  //   beq
  //   addi
endmodule

module JoystickContorller (
  input  [31:0] DataFromBus,
  input  WriteEnableFromBus,
  input  [25:0] AddressFromBus,
  input  [3:0] X,
  input  [3:0] Y,
  output WriteEnableToBus,
  output [31:0] DataToBus
);

  wire and_1_out, and_2_out, comparator_1_eq, comparator_2_eq, not_1_out;
  wire [31:0] bit_extender_1_out, bit_extender_2_out;

  assign bit_extender_1_out = {{28{X[3]}}, X};  // Bit_Extender bit_extender_1
  assign bit_extender_2_out = {{28{Y[3]}}, Y};  // Bit_Extender bit_extender_2
  not not_1 (not_1_out, WriteEnableFromBus);
  Comparator #(.width(26)) comparator_1 (.a(AddressFromBus), .b(26'h3ffff50), .eq(comparator_1_eq));  // open: gt, lt
  Comparator #(.width(26)) comparator_2 (.a(AddressFromBus), .b(26'h3ffff54), .eq(comparator_2_eq));  // open: gt, lt
  and and_1 (and_1_out, not_1_out, comparator_1_eq);
  and and_2 (and_2_out, not_1_out, comparator_2_eq);
  Multiplexer #(.width(32)) multiplexer_1 (
    .in0(bit_extender_1_out), .in1(bit_extender_2_out), .out(DataToBus), .sel(and_2_out));
  or or_1 (WriteEnableToBus, and_1_out, and_2_out);

  // Notes on the sheet:
  //   From Bus
  //   From Joystick
  //   X
  //   Y
  //   ToBus
endmodule

module BuzzerController (
  input  [31:0] DataFromBus,
  input  WEFromBus,
  input  [25:0] AddressFromBus,
  output [13:0] Frequency,
  output [6:0] Volume,
  output EnableSound
);

  wire and_1_out, and_2_out, and_3_out, clock_1_out, clock_2_out, clock_3_out, comparator_1_eq,
       comparator_2_eq, comparator_3_eq, xor_1_out;
  wire [13:0] bit_extender_1_out, register_2_q;

  Bit_Extender #(.in_width(32), .out_width(14)) bit_extender_1 (.in(DataFromBus), .out(bit_extender_1_out));
  Comparator #(.mode("unsigned"), .width(26)) comparator_1 (
    .a(AddressFromBus), .b(26'h3ffff80), .eq(comparator_1_eq));  // open: gt, lt
  Comparator #(.mode("unsigned"), .width(26)) comparator_2 (
    .a(AddressFromBus), .b(26'h3ffff84), .eq(comparator_2_eq));  // open: gt, lt
  Comparator #(.mode("unsigned"), .width(26)) comparator_3 (
    .a(AddressFromBus), .b(26'h3ffff88), .eq(comparator_3_eq));  // open: gt, lt
  and and_1 (and_1_out, WEFromBus, comparator_1_eq);
  Register #(.width(14)) register_1 (
    .D(bit_extender_1_out), .en(and_1_out), .clk(clock_1_out), .Q(Frequency));  // open: clr
  Clock clock_1 (.out(clock_1_out));
  and and_2 (and_2_out, WEFromBus, comparator_3_eq);
  Register #(.width(14)) register_2 (
    .D(bit_extender_1_out), .en(and_3_out), .clk(clock_2_out), .Q(register_2_q));  // open: clr
  Clock clock_2 (.out(clock_2_out));
  and and_3 (and_3_out, WEFromBus, comparator_2_eq);
  Register #(.width(1)) register_3 (.D(xor_1_out), .en(and_2_out), .clk(clock_3_out), .Q(EnableSound));  // open: clr
  xor xor_1 (xor_1_out, EnableSound, and_2_out);
  Clock clock_3 (.out(clock_3_out));
  Bit_Extender #(.in_width(14), .out_width(7)) bit_extender_2 (.in(register_2_q), .out(Volume));
endmodule

module LEDMatrixController (
  input  WE,
  input  [25:0] AddressFromBus,
  input  [31:0] DataFromBus,
  output [4:0] Col1,
  output [4:0] Col2,
  output [4:0] Col3,
  output [4:0] Col4,
  output [4:0] Col5
);

  wire and_1_out, and_2_out, and_3_out, and_4_out, and_5_out, clock_1_out, comparator_1_eq, comparator_2_eq,
       comparator_3_eq, comparator_4_eq, comparator_5_eq;
  wire [4:0] bit_extender_1_out;

  Comparator #(.mode("unsigned"), .width(26)) comparator_1 (
    .a(AddressFromBus), .b(26'h3ffff8c), .eq(comparator_1_eq));  // open: gt, lt
  Comparator #(.mode("unsigned"), .width(26)) comparator_2 (
    .a(AddressFromBus), .b(26'h3ffff90), .eq(comparator_2_eq));  // open: gt, lt
  Comparator #(.mode("unsigned"), .width(26)) comparator_3 (
    .a(AddressFromBus), .b(26'h3ffff94), .eq(comparator_3_eq));  // open: gt, lt
  Comparator #(.mode("unsigned"), .width(26)) comparator_4 (
    .a(AddressFromBus), .b(26'h3ffff98), .eq(comparator_4_eq));  // open: gt, lt
  Comparator #(.mode("unsigned"), .width(26)) comparator_5 (
    .a(AddressFromBus), .b(26'h3ffff9c), .eq(comparator_5_eq));  // open: gt, lt
  Bit_Extender #(.in_width(32), .out_width(5)) bit_extender_1 (.in(DataFromBus), .out(bit_extender_1_out));
  Register #(.width(5)) register_1 (.D(bit_extender_1_out), .en(and_1_out), .clk(clock_1_out), .Q(Col1));  // open: clr
  and and_1 (and_1_out, WE, comparator_1_eq);
  Clock clock_1 (.out(clock_1_out));
  Register #(.width(5)) register_2 (.D(bit_extender_1_out), .en(and_2_out), .clk(clock_1_out), .Q(Col2));  // open: clr
  and and_2 (and_2_out, WE, comparator_2_eq);
  Register #(.width(5)) register_3 (.D(bit_extender_1_out), .en(and_3_out), .clk(clock_1_out), .Q(Col3));  // open: clr
  and and_3 (and_3_out, WE, comparator_3_eq);
  Register #(.width(5)) register_4 (.D(bit_extender_1_out), .en(and_4_out), .clk(clock_1_out), .Q(Col4));  // open: clr
  and and_4 (and_4_out, WE, comparator_4_eq);
  Register #(.width(5)) register_5 (.D(bit_extender_1_out), .en(and_5_out), .clk(clock_1_out), .Q(Col5));  // open: clr
  and and_5 (and_5_out, WE, comparator_5_eq);
endmodule

module OsciController (
  input  WE,
  input  [25:0] AddressFromBus,
  input  [31:0] DataFromBus,
  output Row1,
  output Row2,
  output Row3,
  output Clear,
  output EnableWrite
);

  wire and_1_out, and_2_out, and_3_out, and_5_out, clock_1_out, clock_2_out, clock_3_out, clock_4_out,
       comparator_1_eq, comparator_2_eq, comparator_3_eq, comparator_4_eq, not_1_out, xor_1_out, xor_2_out,
       xor_3_out, xor_4_out;

  Comparator #(.mode("unsigned"), .width(26)) comparator_1 (
    .a(AddressFromBus), .b(26'h3ffffa0), .eq(comparator_1_eq));  // open: gt, lt
  Comparator #(.mode("unsigned"), .width(26)) comparator_2 (
    .a(AddressFromBus), .b(26'h3ffffa4), .eq(comparator_2_eq));  // open: gt, lt
  Comparator #(.mode("unsigned"), .width(26)) comparator_3 (
    .a(AddressFromBus), .b(26'h3ffffa8), .eq(comparator_3_eq));  // open: gt, lt
  Comparator #(.mode("unsigned"), .width(26)) comparator_4 (
    .a(AddressFromBus), .b(26'h3ffffac), .eq(comparator_4_eq));  // open: gt, lt
  not not_1 (not_1_out, WE);
  and and_1 (and_1_out, WE, comparator_1_eq);
  and and_2 (and_2_out, comparator_2_eq, WE);
  xor xor_1 (xor_1_out, Row3, and_3_out);
  and and_3 (and_3_out, comparator_3_eq, WE);
  and and_4 (Clear, WE, comparator_4_eq);
  and and_5 (and_5_out, comparator_4_eq, not_1_out);
  Register #(.width(1)) register_1 (.D(xor_2_out), .en(and_1_out), .clk(clock_1_out), .Q(Row1));  // open: clr
  xor xor_2 (xor_2_out, Row1, and_1_out);
  Clock clock_1 (.out(clock_1_out));
  Register #(.width(1)) register_2 (.D(xor_3_out), .en(and_2_out), .clk(clock_2_out), .Q(Row2));  // open: clr
  xor xor_3 (xor_3_out, Row2, and_2_out);
  Clock clock_2 (.out(clock_2_out));
  Register #(.width(1)) register_3 (.D(xor_1_out), .en(and_3_out), .clk(clock_3_out), .Q(Row3));  // open: clr
  Clock clock_3 (.out(clock_3_out));
  Register #(.width(1)) register_4 (.D(xor_4_out), .en(and_5_out), .clk(clock_4_out), .Q(EnableWrite));  // open: clr
  xor xor_4 (xor_4_out, EnableWrite, and_5_out);
  Clock clock_4 (.out(clock_4_out));
endmodule

module SpeakerController (
  input  [31:0] DataFromBus,
  input  WEFromBus,
  input  [25:0] AddressfromBus,
  output [13:0] Frequency1,
  output [6:0] Volume1,
  output [13:0] F2,
  output [6:0] V2,
  output [13:0] F3,
  output [6:0] V3
);

  wire and_1_out, and_2_out, and_3_out, and_4_out, and_5_out, and_6_out, and_7_out, clock_1_out,
       comparator_1_eq, comparator_2_eq, comparator_3_eq, comparator_4_eq, comparator_5_eq, comparator_6_eq,
       comparator_7_eq;
  wire [6:0] bit_extender_2_out, register_2_q, register_4_q, register_6_q;
  wire [13:0] bit_extender_1_out, register_1_q, register_3_q, register_5_q;

  Bit_Extender #(.in_width(32), .out_width(14)) bit_extender_1 (.in(DataFromBus), .out(bit_extender_1_out));
  Bit_Extender #(.in_width(32), .out_width(7)) bit_extender_2 (.in(DataFromBus), .out(bit_extender_2_out));
  Comparator #(.mode("unsigned"), .width(26)) comparator_1 (
    .a(AddressfromBus), .b(26'h3ffffb0), .eq(comparator_1_eq));  // open: gt, lt
  Comparator #(.mode("unsigned"), .width(26)) comparator_2 (
    .a(AddressfromBus), .b(26'h3ffffb4), .eq(comparator_2_eq));  // open: gt, lt
  Comparator #(.mode("unsigned"), .width(26)) comparator_3 (
    .a(AddressfromBus), .b(26'h3ffffb8), .eq(comparator_3_eq));  // open: gt, lt
  Comparator #(.mode("unsigned"), .width(26)) comparator_4 (
    .a(AddressfromBus), .b(26'h3ffffbc), .eq(comparator_4_eq));  // open: gt, lt
  Comparator #(.mode("unsigned"), .width(26)) comparator_5 (
    .a(AddressfromBus), .b(26'h3ffffc0), .eq(comparator_5_eq));  // open: gt, lt
  Comparator #(.mode("unsigned"), .width(26)) comparator_6 (
    .a(AddressfromBus), .b(26'h3ffffc4), .eq(comparator_6_eq));  // open: gt, lt
  Comparator #(.mode("unsigned"), .width(26)) comparator_7 (
    .a(AddressfromBus), .b(26'h3ffffc8), .eq(comparator_7_eq));  // open: gt, lt
  and and_1 (and_1_out, WEFromBus, comparator_1_eq);
  and and_2 (and_2_out, WEFromBus, comparator_2_eq);
  and and_3 (and_3_out, WEFromBus, comparator_3_eq);
  buf and_4 (and_4_out, comparator_4_eq);  // AND_Gate
  and and_5 (and_5_out, WEFromBus, comparator_5_eq);
  and and_6 (and_6_out, WEFromBus, comparator_6_eq);
  and and_7 (and_7_out, WEFromBus, comparator_7_eq);
  Register #(.width(14)) register_1 (
    .D(bit_extender_1_out), .en(and_1_out), .clk(clock_1_out), .Q(register_1_q));  // open: clr
  Register #(.width(7)) register_2 (
    .D(bit_extender_2_out), .en(and_2_out), .clk(clock_1_out), .Q(register_2_q));  // open: clr
  Register #(.width(14)) register_3 (
    .D(bit_extender_1_out), .en(and_3_out), .clk(clock_1_out), .Q(register_3_q));  // open: clr
  Register #(.width(7)) register_4 (
    .D(bit_extender_2_out), .en(and_4_out), .clk(clock_1_out), .Q(register_4_q));  // open: clr
  Register #(.width(14)) register_5 (
    .D(bit_extender_1_out), .en(and_5_out), .clk(clock_1_out), .Q(register_5_q));  // open: clr
  Register #(.width(7)) register_6 (
    .D(bit_extender_2_out), .en(and_6_out), .clk(clock_1_out), .Q(register_6_q));  // open: clr
  Clock clock_1 (.out(clock_1_out));
  Register #(.width(14)) register_7 (.D(register_1_q), .en(and_7_out), .clk(clock_1_out), .Q(Frequency1));  // open: clr
  Register #(.width(7)) register_8 (.D(register_2_q), .en(and_7_out), .clk(clock_1_out), .Q(Volume1));  // open: clr
  Register #(.width(14)) register_9 (.D(register_3_q), .en(and_7_out), .clk(clock_1_out), .Q(F2));  // open: clr
  Register #(.width(7)) register_10 (.D(register_4_q), .en(and_7_out), .clk(clock_1_out), .Q(V2));  // open: clr
  Register #(.width(14)) register_11 (.D(register_5_q), .en(and_7_out), .clk(clock_1_out), .Q(F3));  // open: clr
  Register #(.width(7)) register_12 (.D(register_6_q), .en(and_7_out), .clk(clock_1_out), .Q(V3));  // open: clr
endmodule
